# Fritzing sketch RFID_LCD_FRONTDOOR (1) (saved by Fritzing 0.9.10b)
breadboards: 1

parts:
  Part1 = Arduino Uno (Rev3)
  LED1 = LED - 5mm [color="Red (633nm)" current=0.030 package="5 mm [THT]"]
  LED2 = LED - 5mm [color="Green (565nm)" current=0.030 package="5 mm [THT]"]
  R1 = Resistor [tolerance=±5% power=0.25 resistance=220 package=THT]
  R2 = Resistor [tolerance=±5% power=0.25 resistance=220 package=THT]
  Part2 = RFID-RC522-v2
  Part3 = LCD1602-I2C
  LED3 = LED - 5mm [color="Yellow (595nm)" current=0.030 package="5 mm [THT]"]
  Mod1 = Amica NodeMCU DEVKIT 1.0
  R3 = Resistor [tolerance=±5% resistance=220 package="2010 [SMD]"]

nets:
  GND: Part1.A0, Part1.GND, R1.Pin_1, R2.Pin_1, Part2.GND, Part3.GND, Mod1.pin2, Mod1.pin_9, Mod1.pin_25, Mod1.pin_29, R3.Pin_1
  N1: Part1.D9_PWM, Part2.SCK
  N2: Part1.D10_PWM/SS, Part2.MOSI
  N3: Part1.D11_PWM/MOSI, Part2.MISO
  N4: Part1.D12/MISO, Part2.SDA
  N5: Part1.A4/SDA, Part3.SDA
  N6: Part1.A5/SCL, Part3.SCL
  N7: Part1.D0/RX, Mod1.pin3
  N8: Part1.D1/TX, Mod1.pin4
  N9: Part1.D2, LED1.anode
  N10: Part1.D4, LED2.anode
  N11: Part1.D5_PWM, Part2.RST
  N12: Part1.D7, LED3.anode
  3V3: Part1.3V3, Part2.3.3V
  5V: Part1.5V, Part3.VCC
  N13: LED1.cathode, R1.Pin_0
  N14: LED2.cathode, R2.Pin_0
  N15: LED3.cathode, R3.Pin_0
  N16: Mod1.pin1, Mod1.pin_10, Mod1.pin_26

custom parts:
  RFID-RC522-v2: A simple China made RFID-RC522 Reader; do check the pin labels, as this is a MFRC522 based clone.
  LCD1602-I2C: A standard character display, usually with 2x16 characters. Comes in many colors with LCM1602 IIC attached.
